# Fritzing sketch talking_clock (saved by Fritzing 1.0.6)
breadboards: 1

parts:
  Mod1 = rpi_pico-tht_1
  S3 = Pushbutton [package="[SMD]"]
  S4 = Pushbutton [package="[SMD]"]
  S5 = Pushbutton [package="[SMD]"]
  Part1 = RTC DS3231
  microSD1 = MicroSD Card Module
  Part2 = Adafruit MAX98357A I2S 3W Class D Amplifier [part_number="Adafruit #3006"]

nets:
  N1: Mod1.connector2, Part1.SDA
  N2: Mod1.connector3, Part1.SCL
  N3: Mod1.connector13, Part2.DIN
  N4: Mod1.connector14, Part2.BCLK
  N5: Mod1.connector15, Part2.LRCLK
  N6: Mod1.connector16, Part2.GAIN
  N7: Mod1.connector20, microSD1.MISO
  N8: Mod1.connector21, microSD1.CS
  N9: Mod1.connector23, microSD1.SCK
  N10: Mod1.connector24, microSD1.MOSI
  N11: Mod1.connector35, Part1.VCC
  GND: Mod1.connector37, S3.Pin_3, S3.Pin_4, S4.Pin_3, S4.Pin_4, S5.Pin_3, S5.Pin_4, Part1.GND, microSD1.GND, Part2.GND
  VCC: Mod1.connector39, microSD1.VCC, Part2.VIN
  N12: S3.Pin_1, S3.Pin_2
  N13: S4.Pin_1, S4.Pin_2
  N14: S5.Pin_1, S5.Pin_2

custom parts:
  RTC DS3231: DS3231 with akku
  Adafruit MAX98357A I2S 3W Class D Amplifier: Listen to this good news - we now have an all in one digital audio amp breakout board that works incredibly well with the Raspberry Pi! If you're looking for an easy and low cost way to get you digital sound files bumpin' then the MAX08357 I2S Amp Breakout is for you. It takes standard I2S digital audio input and, not only decodes it into analog, but also amplifies it directly into a speaker.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
